# Fritzing sketch autogreens (saved by Fritzing 0.9.3b)

parts:
  U1 = ESP32S-HiLetgo [part_number=ESP32S-HiLetgo]
  Componente1 = Soil Moisture Sensor
  RHT1 = Humidity and Temperature Sensor RHT03
  Water_Level_Sensor1 = Water Level Sensor

nets:
  N1: U1.GPIO32, Componente1.SIG
  GND: U1.GND, Componente1.GND, RHT1.GND_1, Water_Level_Sensor1.GND
  N2: U1.GPIO11, RHT1.Data-signal
  VCC: U1.VIN, Componente1.VCC, RHT1.Vcc, Water_Level_Sensor1.VCC
  N3: U1.GPIO7, Water_Level_Sensor1.SIG

custom parts:
  ESP32S-HiLetgo: HiLetgo ESP-WROOM-32 ESP32 ESP-32S Development Board 2.4GHz Dual-Mode WiFi + Bluetooth Dual Cores Microcontroller The ESP32 integrated with Antenna switches, RF Balun, power amplifiers, low-noise amplifiers, filters, and management modules, and the entire solution occupies the least area of PCB. 2.4 GHz Wi-Fi plus Bluetooth dual-mode chip, with TSMC Ultra-low power consumption 40nm technology,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
  Water Level Sensor: A water level sensor. This sensor operates at 3V to 5V. The Sig (signal) pin outputs an analogue signal that is in proportion to the amount of water in contact with the sensor.
